# Fritzing sketch kim-jian-assignment-wifi (saved by Fritzing 0.9.4)
breadboards: 1

parts:
  S3 = Momentary Switch [package=ksa_sealed_tac_switch]
  S4 = Momentary Switch [package=ksa_sealed_tac_switch]
  S5 = Momentary Switch [package=ksa_sealed_tac_switch]
  S6 = Momentary Switch [package=ksa_sealed_tac_switch]
  LED1 = LED - 3mm [color="Red (633nm)" package="3 mm [THT]"]
  LED2 = LED - 3mm [color="Green (565nm)" package="3 mm [THT]"]
  LED3 = LED - 3mm [color="Blue (470nm)" package="3 mm [THT]"]
  LED4 = LED - 3mm [color="Yellow (592nm)" package="3 mm [THT]"]
  R1 = Resistor [tolerance=±5% resistance=330 package=THT]
  R2 = Resistor [tolerance=±5% resistance=330 package=THT]
  R3 = Resistor [tolerance=±5% resistance=330 package=THT]
  R4 = Resistor [tolerance=±5% resistance=330 package=THT]
  R5 = Resistor [tolerance=±5% resistance=220 package=THT]
  R6 = Resistor [tolerance=±5% resistance=220 package=THT]
  R7 = Resistor [tolerance=±5% resistance=220 package=THT]
  R8 = Resistor [tolerance=±5% resistance=220 package=THT]
  J1 = Piezo Speaker
  Adafruit_HUZZAH_ESP8266_Breakout2 = Adafruit HUZZAH ESP8266 Breakout [part_number=2471]

nets:
  N1: S3.3, S4.3, S5.3, S6.3, R1.Pin_0, R2.Pin_0, R3.Pin_0, R4.Pin_0, J1.pin1, Adafruit_HUZZAH_ESP8266_Breakout2.GND
  N2: S3.4, R5.Pin_0
  N3: S4.2, Adafruit_HUZZAH_ESP8266_Breakout2.#2
  N4: S4.4, R6.Pin_0
  N5: S5.2, Adafruit_HUZZAH_ESP8266_Breakout2.#5
  N6: S5.4, R7.Pin_0
  N7: S6.2, Adafruit_HUZZAH_ESP8266_Breakout2.#_3
  N8: S6.4, R8.Pin_0
  N9: LED1.cathode, R1.Pin_1
  N10: LED1.anode, Adafruit_HUZZAH_ESP8266_Breakout2.#0
  N11: LED2.cathode, R2.Pin_1
  N12: LED2.anode, Adafruit_HUZZAH_ESP8266_Breakout2.#12
  N13: LED3.cathode, R3.Pin_1
  N14: LED3.anode, Adafruit_HUZZAH_ESP8266_Breakout2.#15
  N15: LED4.cathode, R4.Pin_1
  N16: LED4.anode, Adafruit_HUZZAH_ESP8266_Breakout2.#16
  N17: R5.Pin_1, R6.Pin_1, R7.Pin_1, R8.Pin_1, Adafruit_HUZZAH_ESP8266_Breakout2.3V

custom parts:
  Adafruit HUZZAH ESP8266 Breakout: The HUZZAH ESP8266 breakout is what we designed to make working with this chip super easy and a lot of fun. We took a certified module with an onboard antenna, and plenty of pins, and soldered it onto our designed breakout PCBs. We added in: Reset button, User button that can also put the chip into bootloading mode, Red LED you can blink Level shifting on the UART and reset pin 3.3V out, 500mA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
