# Fritzing sketch Simon Game (saved by Fritzing 0.9.4)
breadboards: 1

parts:
  Adafruit_HUZZAH_ESP8266_Breakout1 = Adafruit HUZZAH ESP8266 Breakout [part_number=2471]
  S1 = Momentary Switch [package=ksa_sealed_tac_switch]
  S2 = Momentary Switch [package=ksa_sealed_tac_switch]
  S3 = Momentary Switch [package=ksa_sealed_tac_switch]
  J1 = Piezo Speaker
  LED1 = LED - 3mm [color="Blue (430nm)" package="3 mm [THT]"]
  LED2 = LED - 3mm [color="Red (633nm)" package="3 mm [THT]"]
  LED3 = LED - 3mm [color="Green (555nm)" package="3 mm [THT]"]
  R1 = Resistor [tolerance=±5% resistance=220 package=THT]
  R2 = Resistor [tolerance=±5% resistance=220 package=THT]
  R3 = Resistor [tolerance=±5% resistance=220 package=THT]
  R4 = Resistor [tolerance=±5% resistance=330 package=THT]
  R5 = Resistor [tolerance=±5% resistance=330 package=THT]
  R6 = Resistor [tolerance=±5% resistance=330 package=THT]

nets:
  N1: Adafruit_HUZZAH_ESP8266_Breakout1.GND, J1.pin1, R4.Pin_1, R5.Pin_1, R6.Pin_1
  N2: Adafruit_HUZZAH_ESP8266_Breakout1.#13, LED1.anode
  N3: Adafruit_HUZZAH_ESP8266_Breakout1.#14, J1.pin2
  N4: Adafruit_HUZZAH_ESP8266_Breakout1.#5, S3.1
  N5: Adafruit_HUZZAH_ESP8266_Breakout1.#4, S2.1
  N6: Adafruit_HUZZAH_ESP8266_Breakout1.#0, LED3.anode
  N7: Adafruit_HUZZAH_ESP8266_Breakout1.#2, S1.1
  N8: Adafruit_HUZZAH_ESP8266_Breakout1.#15, LED2.anode
  N9: Adafruit_HUZZAH_ESP8266_Breakout1.3V, R1.Pin_0, R2.Pin_0, R3.Pin_0
  N10: S1.3, R2.Pin_1
  N11: S2.3, R1.Pin_1
  N12: S3.3, R3.Pin_1
  N13: LED1.cathode, R4.Pin_0
  N14: LED2.cathode, R5.Pin_0
  N15: LED3.cathode, R6.Pin_0
